# Fritzing sketch Schema (saved by Fritzing 0.9.3b)
breadboards: 2

parts:
  LED1 = smd LED [color="Red (635nm)" package="1206 [SMD]"]
  R1 = Resistor [tolerance=±5% resistance=220 package="0603 [SMD]"]
  LED2 = smd LED [color="Yellow (595nm)" package="1206 [SMD]"]
  LED3 = smd LED [color="Green (555nm)" package="1206 [SMD]"]
  R2 = Resistor [tolerance=±5% resistance=220 package="0603 [SMD]"]
  R3 = Resistor [tolerance=±5% resistance=220 package="0603 [SMD]"]
  S8 = Pushbutton [package="[THT]"]
  LED4 = smd LED [color="Blue (430nm)" package="1206 [SMD]"]
  R4 = Resistor [tolerance=±5% resistance=220 package="0603 [SMD]"]
  Part1 = Arduino Uno (Rev3)
  S9 = Pushbutton [package="[THT]"]
  S10 = Pushbutton [package="[THT]"]
  S11 = Pushbutton [package="[THT]"]

nets:
  N1: LED1.cathode, LED2.cathode, LED3.cathode, S8.Pin_3, S8.Pin_4, LED4.cathode, Part1.GND, S9.Pin_3, S9.Pin_4, S10.Pin_3, S10.Pin_4, S11.Pin_3, S11.Pin_4
  N2: LED1.anode, R1.Pin_1
  N3: R1.Pin_0, Part1.D4
  N4: LED2.anode, R2.Pin_1
  N5: LED3.anode, R3.Pin_1
  N6: R2.Pin_0, Part1.D5_PWM
  N7: R3.Pin_0, Part1.D6_PWM
  N8: S8.Pin_1, S8.Pin_2, Part1.D11_PWM/MOSI
  N9: LED4.anode, R4.Pin_1
  N10: R4.Pin_0, Part1.D7
  N11: Part1.D8, S11.Pin_1, S11.Pin_2
  N12: Part1.D9_PWM, S10.Pin_1, S10.Pin_2
  N13: Part1.D10_PWM/SS, S9.Pin_1, S9.Pin_2

notes:
  RED
  YELLOW
  GREEN
  BLUE
